// Logisim project FCPU01.circ as structural Verilog: 21 circuits, main circuit TEST
module FCPU_01 (
);

  PROCESSOR processor_1 ();  // open: CLR, C_O, S8, S7, S6, S5, S4, S3, S2, S1, S0, out_12
endmodule

module PROCESSOR (
  input  CLR,
  output C_O,
  output S8,
  output S7,
  output S6,
  output S5,
  output S4,
  output S3,
  output S2,
  output S1,
  output S0,
  output [11:0] out_12
);

  wire clk_1_clk_out, mcpg_control_1_b0, mcpg_control_1_b1, mcpg_control_1_b2, mcpg_control_1_b3,
       mcpg_control_1_b4, mcpg_control_1_b5, mcpg_control_1_b6, mcpg_control_1_b7, mcpg_control_1_b8,
       mcpg_control_1_b9, mcpg_control_1_b10, mcpg_control_1_b11, not_1_out, pc_chip_1_c_out,
       ring_counter_1_t1, ring_counter_1_t3;
  wire [3:0] ir_chip_1_opcode, mar_1_d_out;
  wire [7:0] accumulator_1_q_alu, latch_1_q_out, reg_b_1_q_out, sram_chip_1_ram_out;

  not not_1 (not_1_out, clk_1_clk_out);
  MAR mar_1 (
    .D_IN(sram_chip_1_ram_out), .EN(mcpg_control_1_b2), .CLK(clk_1_clk_out), .n_RESET(CLR),
    .D_OUT(mar_1_d_out));  // open: EA
  SRAM_CHIP sram_chip_1 (
    .ADD_IN(mar_1_d_out), .SEL(mcpg_control_1_b3), .RAM_OUT(sram_chip_1_ram_out));  // open: DATA_IN, EA
  IR_CHIP ir_chip_1 (
    .D_IN(sram_chip_1_ram_out), .EA(mcpg_control_1_b5), .EN(mcpg_control_1_b4), .CLK(clk_1_clk_out),
    .n_RESET(CLR), .OPCODE(ir_chip_1_opcode), .operand(sram_chip_1_ram_out));  // open: D_OUT
  MCPG_CONTROL mcpg_control_1 (
    .T1(ring_counter_1_t1), .T3(ring_counter_1_t3), .OUT_ROM(out_12), .IN_ROM(ir_chip_1_opcode),
    .B11(mcpg_control_1_b11), .B10(mcpg_control_1_b10), .B9(mcpg_control_1_b9), .B8(mcpg_control_1_b8),
    .B7(mcpg_control_1_b7), .B6(mcpg_control_1_b6), .B5(mcpg_control_1_b5), .B4(mcpg_control_1_b4),
    .B3(mcpg_control_1_b3), .B2(mcpg_control_1_b2), .B1(mcpg_control_1_b1), .B0(mcpg_control_1_b0));  // open: CLK
  Ring_Counter ring_counter_1 (
    .CLK(not_1_out), .reset(CLR), .T1(ring_counter_1_t1), .T3(ring_counter_1_t3));  // open: RC_OUT
  CLK clk_1 (.CLK_OUT(clk_1_clk_out));  // open: TOGGLE
  PC_chip pc_chip_1 (
    .EN(mcpg_control_1_b0), .IN_BUS(sram_chip_1_ram_out), .EA(mcpg_control_1_b1), .CLR(CLR),
    .CLK(clk_1_clk_out), .OUT_BUS(sram_chip_1_ram_out), .C_OUT(pc_chip_1_c_out));  // open: LOAD
  LED PC_FULL (.in(pc_chip_1_c_out));
  Hex_Digit_Display hex_digit_display_1 (.value(latch_1_q_out[3:0]));  // open: dp
  Hex_Digit_Display hex_digit_display_2 (.value(latch_1_q_out[7:4]));  // open: dp
  accumulator accumulator_1 (
    .LOAD(mcpg_control_1_b6), .EA(mcpg_control_1_b7), .D_IN(sram_chip_1_ram_out), .CLK(clk_1_clk_out),
    .CLR(CLR), .Q_OUT(sram_chip_1_ram_out), .Q_ALU(accumulator_1_q_alu));
  ALU_SAP01 alu_sap01_1 (
    .En(mcpg_control_1_b9), .CTR(mcpg_control_1_b8), .A_in(accumulator_1_q_alu), .B_in(reg_b_1_q_out),
    .C_out(C_O), .ZF(S8), .S7(S7), .S6(S6), .S5(S5), .S4(S4), .S3(S3), .S2(S2), .S1(S1), .S0(S0),
    .ALU_out(sram_chip_1_ram_out));
  REG_B reg_b_1 (
    .LOAD(mcpg_control_1_b10), .D_IN(sram_chip_1_ram_out), .CLK(clk_1_clk_out), .CLR(CLR),
    .Q_OUT(reg_b_1_q_out));
  LATCH latch_1 (
    .Enabled(mcpg_control_1_b11), .D_IN(sram_chip_1_ram_out), .Reset(CLR), .Q_OUT(latch_1_q_out));  // open: EA
endmodule

module CLK (
  input  TOGGLE,
  output CLK_OUT
);

  wire ASTABLE_TIMER_out, MANUAL_out;

  Button MANUAL (.out(MANUAL_out));
  Clock ASTABLE_TIMER (.out(ASTABLE_TIMER_out));
  Multiplexer multiplexer_1 (.in0(MANUAL_out), .in1(ASTABLE_TIMER_out), .out(CLK_OUT), .sel(TOGGLE));
endmodule

module TEST (
);

  // NoConnect on nothing
endmodule

module MAR (
  input  [7:0] D_IN,
  input  EN,
  input  EA,
  input  CLK,
  input  n_RESET,
  output [3:0] D_OUT
);

  wire not_1_out, undriven;
  wire [3:0] register_1_q;

  not not_1 (not_1_out, n_RESET);
  Register #(.width(4)) register_1 (.D(D_IN[3:0]), .en(EN), .clk(CLK), .Q(register_1_q), .clr(not_1_out));
  assign D_OUT = undriven ? register_1_q : 4'bz;  // Controlled_Buffer controlled_buffer_1
endmodule

module PC_chip (
  input  EN,
  input  LOAD,
  input  [7:0] IN_BUS,
  input  EA,
  input  CLR,
  input  CLK,
  output [7:0] OUT_BUS,
  output C_OUT
);

  wire and_1_out, and_2_out, and_3_out, and_4_out, and_5_out, and_6_out, and_7_out, and_8_out, and_9_out,
       and_10_out, and_11_out, and_12_out, and_13_out, buffer_2_out, not_1_out, not_2_out, not_3_out,
       not_4_out, not_5_out, not_6_out, not_7_out, or_1_out, or_2_out, or_3_out, or_4_out, or_5_out,
       or_6_out, or_7_out, or_8_out;
  wire [3:0] buffer_1_out, undriven;
  wire [3:1] j_k_ff_2_q;
  wire [7:0] bit_extender_2_out;

  assign buffer_1_out = undriven;  // Buffer buffer_1, 4 bits wide
  assign IN_BUS = {{4{buffer_1_out[3]}}, buffer_1_out};  // Bit_Extender bit_extender_1
  not not_1 (not_1_out, LOAD);
  not not_2 (not_2_out, undriven[0]);
  not not_3 (not_3_out, undriven[1]);
  not not_4 (not_4_out, undriven[2]);
  not not_5 (not_5_out, undriven[3]);
  buf buffer_2 (buffer_2_out, CLR);
  not not_6 (not_6_out, CLK);
  and and_1 (and_1_out, EN, not_1_out);
  not not_7 (not_7_out, not_1_out);
  and and_2 (and_2_out, not_7_out, undriven[0]);
  and and_3 (and_3_out, not_7_out, not_2_out);
  and and_4 (and_4_out, not_7_out, undriven[1]);
  and and_5 (and_5_out, not_7_out, not_3_out);
  and and_6 (and_6_out, not_7_out, undriven[2]);
  and and_7 (and_7_out, not_7_out, not_4_out);
  and and_8 (and_8_out, not_7_out, undriven[3]);
  and and_9 (and_9_out, not_7_out, not_5_out);
  or or_1 (or_1_out, and_2_out, and_1_out);
  or or_2 (or_2_out, and_3_out, and_1_out);
  and and_10 (and_10_out, j_k_ff_2_q[2], and_1_out);
  and and_11 (and_11_out, j_k_ff_2_q[1], and_1_out);
  or or_3 (or_3_out, and_4_out, and_10_out);
  or or_4 (or_4_out, and_6_out, and_11_out);
  and and_12 (and_12_out, and_1_out, j_k_ff_2_q[1]);
  or or_5 (or_5_out, and_10_out, and_5_out);
  or or_6 (or_6_out, and_11_out, and_7_out);
  or or_7 (or_7_out, and_8_out, and_12_out);
  or or_8 (or_8_out, and_12_out, and_9_out);
  J_K_Flip_Flop j_k_ff_1 (
    .J(or_1_out), .K(or_2_out), .clk(not_6_out), .Q(j_k_ff_2_q[2]), .reset(buffer_2_out));  // open: Qn, preset
  J_K_Flip_Flop j_k_ff_2 (
    .J(or_3_out), .K(or_5_out), .clk(not_6_out), .Q(j_k_ff_2_q[1]), .reset(buffer_2_out));  // open: Qn, preset
  J_K_Flip_Flop j_k_ff_3 (
    .J(or_4_out), .K(or_6_out), .clk(not_6_out), .Q(j_k_ff_2_q[2]), .reset(buffer_2_out));  // open: Qn, preset
  J_K_Flip_Flop j_k_ff_4 (
    .J(or_7_out), .K(or_8_out), .clk(not_6_out), .Q(j_k_ff_2_q[3]), .reset(buffer_2_out));  // open: Qn, preset
  buf and_13 (and_13_out, and_1_out);  // AND_Gate
  assign OUT_BUS = EA ? bit_extender_2_out : 8'bz;  // Controlled_Buffer controlled_buffer_1
  assign bit_extender_2_out = {{4{j_k_ff_2_q[3]}}, {j_k_ff_2_q, j_k_ff_2_q[2]}};  // Bit_Extender bit_extender_2
endmodule

module LATCH (
  input  Enabled,
  input  [7:0] D_IN,
  input  EA,
  input  Reset,
  output [7:0] Q_OUT
);

  wire [7:0] controlled_buffer_1_out, d_ff_1_q, undriven;

  assign D_IN = undriven;  // Buffer buffer_1, 8 bits wide
  D_Flip_Flop #(.trigger("high")) d_ff_1 (
    .D(undriven[0]), .clk(Enabled), .Q(d_ff_1_q[0]), .reset(Reset));  // open: Qn, preset
  D_Flip_Flop #(.trigger("high")) d_ff_2 (
    .D(undriven[1]), .clk(Enabled), .Q(d_ff_1_q[1]), .reset(Reset));  // open: Qn, preset
  D_Flip_Flop #(.trigger("high")) d_ff_3 (
    .D(undriven[2]), .clk(Enabled), .Q(d_ff_1_q[2]), .reset(Reset));  // open: Qn, preset
  D_Flip_Flop #(.trigger("high")) d_ff_4 (
    .D(undriven[3]), .clk(Enabled), .Q(d_ff_1_q[3]), .reset(Reset));  // open: Qn, preset
  D_Flip_Flop #(.trigger("high")) d_ff_5 (
    .D(undriven[4]), .clk(Enabled), .Q(d_ff_1_q[4]), .reset(Reset));  // open: Qn, preset
  D_Flip_Flop #(.trigger("high")) d_ff_6 (
    .D(undriven[5]), .clk(Enabled), .Q(d_ff_1_q[5]), .reset(Reset));  // open: Qn, preset
  D_Flip_Flop #(.trigger("high")) d_ff_7 (
    .D(undriven[6]), .clk(Enabled), .Q(d_ff_1_q[6]), .reset(Reset));  // open: Qn, preset
  D_Flip_Flop #(.trigger("high")) d_ff_8 (
    .D(undriven[7]), .clk(Enabled), .Q(d_ff_1_q[7]), .reset(Reset));  // open: Qn, preset
  assign controlled_buffer_1_out = EA ? d_ff_1_q : 8'bz;  // Controlled_Buffer controlled_buffer_1

  // Notes on the sheet:
  //   8bit latch
endmodule

module FA_1BIT (
  input  A,
  input  B,
  input  C_In,
  output Sum,
  output C_out
);

  wire and_1_out, and_2_out, xor_1_out;

  xor xor_1 (xor_1_out, A, B);
  xor xor_2 (Sum, xor_1_out, C_In);
  and and_1 (and_1_out, C_In, xor_1_out);
  and and_2 (and_2_out, A, B);
  or or_1 (C_out, and_1_out, and_2_out);

  // Notes on the sheet:
  //   1bit_adder
endmodule

module FA_4BIT (
  input  A0,
  input  S0,
  input  B0,
  input  C_in,
  input  A1,
  input  S1,
  input  B1,
  input  A2,
  input  S2,
  input  B2,
  input  A3,
  input  S3,
  input  B3,
  input  C_out
);

  wire fa_1bit_1_c_out, fa_1bit_2_c_out, fa_1bit_3_c_out;

  FA_1BIT fa_1bit_1 (.A(A0), .B(B0), .C_In(C_in), .Sum(S0), .C_out(fa_1bit_1_c_out));
  FA_1BIT fa_1bit_2 (.A(A1), .B(B1), .C_In(fa_1bit_1_c_out), .Sum(S1), .C_out(fa_1bit_2_c_out));
  FA_1BIT fa_1bit_3 (.A(A2), .B(B2), .C_In(fa_1bit_2_c_out), .Sum(S2), .C_out(fa_1bit_3_c_out));
  FA_1BIT fa_1bit_4 (.A(A3), .B(B3), .C_In(fa_1bit_3_c_out), .Sum(S3), .C_out(C_out));
endmodule

module add_sub4BIT (
  input  CTR,
  input  AO,
  input  B0,
  input  A1,
  input  B1,
  input  A2,
  input  B2,
  input  A3,
  input  B3,
  output S0,
  output S1,
  output S2,
  output S3,
  output C_out
);

  wire fa_1bit_1_c_out, fa_1bit_2_c_out, fa_1bit_3_c_out, xor_1_out, xor_2_out, xor_3_out, xor_4_out;

  xor xor_1 (xor_1_out, CTR, B0);
  xor xor_2 (xor_2_out, CTR, B1);
  xor xor_3 (xor_3_out, CTR, B2);
  xor xor_4 (xor_4_out, CTR, B3);
  FA_1BIT fa_1bit_1 (.A(AO), .B(xor_1_out), .C_In(CTR), .Sum(S0), .C_out(fa_1bit_1_c_out));
  FA_1BIT fa_1bit_2 (.A(A1), .B(xor_2_out), .C_In(fa_1bit_1_c_out), .Sum(S1), .C_out(fa_1bit_2_c_out));
  FA_1BIT fa_1bit_3 (.A(A2), .B(xor_3_out), .C_In(fa_1bit_2_c_out), .Sum(S2), .C_out(fa_1bit_3_c_out));
  FA_1BIT fa_1bit_4 (.A(A3), .B(xor_4_out), .C_In(fa_1bit_3_c_out), .Sum(S3), .C_out(C_out));
endmodule

module accumulator (
  input  LOAD,
  input  EA,
  input  [7:0] D_IN,
  input  CLK,
  input  CLR,
  output [7:0] Q_OUT,
  output [7:0] Q_ALU
);

  wire and_1_out, and_2_out, and_3_out, and_4_out, and_5_out, and_6_out, and_7_out, and_8_out, and_9_out,
       and_10_out, and_11_out, and_12_out, and_13_out, and_14_out, and_15_out, and_16_out, not_1_out,
       not_2_out, not_3_out, not_4_out, not_5_out, not_6_out, not_7_out, not_8_out, or_1_out, or_2_out,
       or_3_out, or_4_out, or_6_out, or_7_out, or_8_out, undriven_2;
  wire [7:0] undriven;

  Controlled_Buffer #(.width(8)) controlled_buffer_1 (.in(undriven), .out(D_IN));  // open: en
  not not_1 (not_1_out, LOAD);
  not not_2 (not_2_out, LOAD);
  not not_3 (not_3_out, LOAD);
  not not_4 (not_4_out, LOAD);
  not not_5 (not_5_out, LOAD);
  not not_6 (not_6_out, LOAD);
  not not_7 (not_7_out, LOAD);
  not not_8 (not_8_out, LOAD);
  and and_1 (and_1_out, Q_ALU[5], not_5_out);
  and and_2 (and_2_out, LOAD, undriven[5]);
  and and_3 (and_3_out, Q_ALU[6], not_6_out);
  and and_4 (and_4_out, LOAD, undriven[6]);
  and and_5 (and_5_out, Q_ALU[7], not_7_out);
  and and_6 (and_6_out, LOAD, undriven[7]);
  and and_7 (and_7_out, Q_ALU[0], not_8_out);
  and and_8 (and_8_out, LOAD, undriven[0]);
  and and_9 (and_9_out, Q_ALU[1], not_1_out);
  and and_10 (and_10_out, LOAD, undriven[1]);
  and and_11 (and_11_out, Q_ALU[2], not_2_out);
  and and_12 (and_12_out, LOAD, undriven[2]);
  and and_13 (and_13_out, Q_ALU[3], not_3_out);
  and and_14 (and_14_out, LOAD, undriven[3]);
  and and_15 (and_15_out, Q_ALU[4], not_4_out);
  and and_16 (and_16_out, LOAD, undriven[4]);
  or or_1 (or_1_out, and_7_out, and_8_out);
  or or_2 (or_2_out, and_9_out, and_10_out);
  or or_3 (or_3_out, and_11_out, and_12_out);
  or or_4 (or_4_out, and_13_out, and_14_out);
  or or_5 (CLR, and_15_out, and_16_out);
  or or_6 (or_6_out, and_1_out, and_2_out);
  or or_7 (or_7_out, and_3_out, and_4_out);
  or or_8 (or_8_out, and_5_out, and_6_out);
  D_Flip_Flop d_ff_1 (.D(or_1_out), .clk(CLK), .Q(Q_ALU[0]), .reset(CLR));  // open: Qn, preset
  D_Flip_Flop d_ff_2 (.D(or_2_out), .clk(CLK), .Q(Q_ALU[1]), .reset(CLR));  // open: Qn, preset
  D_Flip_Flop d_ff_3 (.D(or_3_out), .clk(CLK), .Q(Q_ALU[2]), .reset(CLR));  // open: Qn, preset
  D_Flip_Flop d_ff_4 (.D(or_4_out), .clk(CLK), .Q(Q_ALU[3]), .reset(CLR));  // open: Qn, preset
  D_Flip_Flop d_ff_5 (.D(CLR), .clk(CLK), .Q(Q_ALU[4]), .reset(CLR));  // open: Qn, preset
  D_Flip_Flop d_ff_6 (.D(or_6_out), .clk(CLK), .Q(Q_ALU[5]), .reset(CLR));  // open: Qn, preset
  D_Flip_Flop d_ff_7 (.D(or_7_out), .clk(CLK), .Q(Q_ALU[6]), .reset(CLR));  // open: Qn, preset
  D_Flip_Flop d_ff_8 (.D(or_8_out), .clk(CLK), .Q(Q_ALU[7]), .reset(CLR));  // open: Qn, preset
  assign Q_OUT = undriven_2 ? Q_ALU : 8'bz;  // Controlled_Buffer controlled_buffer_2
endmodule

module REG_B (
  input  LOAD,
  input  [7:0] D_IN,
  input  CLK,
  input  CLR,
  output [7:0] Q_OUT
);

  wire and_1_out, and_2_out, and_3_out, and_4_out, and_5_out, and_6_out, and_7_out, and_8_out, and_9_out,
       and_10_out, and_11_out, and_12_out, and_13_out, and_14_out, and_15_out, and_16_out, not_1_out,
       not_2_out, not_3_out, not_4_out, not_5_out, not_6_out, not_7_out, not_8_out, or_1_out, or_2_out,
       or_3_out, or_4_out, or_6_out, or_7_out, or_8_out;
  wire [7:0] d_ff_1_q, undriven;

  assign D_IN = undriven;  // Buffer buffer_1, 8 bits wide
  not not_1 (not_1_out, LOAD);
  not not_2 (not_2_out, LOAD);
  not not_3 (not_3_out, LOAD);
  not not_4 (not_4_out, LOAD);
  not not_5 (not_5_out, LOAD);
  not not_6 (not_6_out, LOAD);
  not not_7 (not_7_out, LOAD);
  not not_8 (not_8_out, LOAD);
  and and_1 (and_1_out, d_ff_1_q[5], not_5_out);
  and and_2 (and_2_out, LOAD, undriven[5]);
  and and_3 (and_3_out, d_ff_1_q[6], not_6_out);
  and and_4 (and_4_out, LOAD, undriven[6]);
  and and_5 (and_5_out, d_ff_1_q[7], not_7_out);
  and and_6 (and_6_out, LOAD, undriven[7]);
  and and_7 (and_7_out, d_ff_1_q[0], not_8_out);
  and and_8 (and_8_out, LOAD, undriven[0]);
  and and_9 (and_9_out, d_ff_1_q[1], not_1_out);
  and and_10 (and_10_out, LOAD, undriven[1]);
  and and_11 (and_11_out, d_ff_1_q[2], not_2_out);
  and and_12 (and_12_out, LOAD, undriven[2]);
  and and_13 (and_13_out, d_ff_1_q[3], not_3_out);
  and and_14 (and_14_out, LOAD, undriven[3]);
  and and_15 (and_15_out, d_ff_1_q[4], not_4_out);
  and and_16 (and_16_out, LOAD, undriven[4]);
  or or_1 (or_1_out, and_7_out, and_8_out);
  or or_2 (or_2_out, and_9_out, and_10_out);
  or or_3 (or_3_out, and_11_out, and_12_out);
  or or_4 (or_4_out, and_13_out, and_14_out);
  or or_5 (CLR, and_15_out, and_16_out);
  or or_6 (or_6_out, and_1_out, and_2_out);
  or or_7 (or_7_out, and_3_out, and_4_out);
  or or_8 (or_8_out, and_5_out, and_6_out);
  D_Flip_Flop d_ff_1 (.D(or_1_out), .clk(CLK), .Q(d_ff_1_q[0]), .reset(CLR));  // open: Qn, preset
  D_Flip_Flop d_ff_2 (.D(or_2_out), .clk(CLK), .Q(d_ff_1_q[1]), .reset(CLR));  // open: Qn, preset
  D_Flip_Flop d_ff_3 (.D(or_3_out), .clk(CLK), .Q(d_ff_1_q[2]), .reset(CLR));  // open: Qn, preset
  D_Flip_Flop d_ff_4 (.D(or_4_out), .clk(CLK), .Q(d_ff_1_q[3]), .reset(CLR));  // open: Qn, preset
  D_Flip_Flop d_ff_5 (.D(CLR), .clk(CLK), .Q(d_ff_1_q[4]), .reset(CLR));  // open: Qn, preset
  D_Flip_Flop d_ff_6 (.D(or_6_out), .clk(CLK), .Q(d_ff_1_q[5]), .reset(CLR));  // open: Qn, preset
  D_Flip_Flop d_ff_7 (.D(or_7_out), .clk(CLK), .Q(d_ff_1_q[6]), .reset(CLR));  // open: Qn, preset
  D_Flip_Flop d_ff_8 (.D(or_8_out), .clk(CLK), .Q(d_ff_1_q[7]), .reset(CLR));  // open: Qn, preset
  assign Q_OUT = d_ff_1_q;  // Buffer buffer_2, 8 bits wide
endmodule

module ALU_SAP01 (
  input  En,
  input  CTR,
  input  [7:0] A_in,
  input  [7:0] B_in,
  output C_out,
  output ZF,
  output S7,
  output S6,
  output S5,
  output S4,
  output S3,
  output S2,
  output S1,
  output S0,
  output [7:0] ALU_out
);

  wire add_sub4bit_1_c_out;

  add_sub4BIT add_sub4bit_1 (
    .CTR(CTR), .AO(A_in[0]), .B0(B_in[0]), .A1(A_in[1]), .B1(B_in[1]), .A2(A_in[2]), .B2(B_in[2]),
    .A3(A_in[3]), .B3(B_in[3]), .S0(S0), .S1(S1), .S2(S2), .S3(S3), .C_out(add_sub4bit_1_c_out));
  add_sub4BIT add_sub4bit_2 (
    .CTR(add_sub4bit_1_c_out), .AO(A_in[4]), .B0(B_in[4]), .A1(A_in[5]), .B1(B_in[5]), .A2(A_in[6]),
    .B2(B_in[6]), .A3(A_in[7]), .B3(B_in[7]), .S0(S4), .S1(S5), .S2(S6), .S3(S7), .C_out(C_out));
  nor nor_1 (ZF, S7, S6, S5, S4, S3, S2, S1, S0);
  assign ALU_out[7] = En ? S7 : 1'bz;  // Controlled_Buffer controlled_buffer_1
  assign ALU_out[6] = En ? S6 : 1'bz;  // Controlled_Buffer controlled_buffer_2
  assign ALU_out[5] = En ? S5 : 1'bz;  // Controlled_Buffer controlled_buffer_3
  assign ALU_out[6] = En ? S4 : 1'bz;  // Controlled_Buffer controlled_buffer_4
  assign ALU_out[3] = En ? S3 : 1'bz;  // Controlled_Buffer controlled_buffer_5
  assign ALU_out[2] = En ? S2 : 1'bz;  // Controlled_Buffer controlled_buffer_6
  assign ALU_out[1] = En ? S1 : 1'bz;  // Controlled_Buffer controlled_buffer_7
  assign ALU_out[0] = En ? S0 : 1'bz;  // Controlled_Buffer controlled_buffer_8

  assign ALU_out[4] = ALU_out[6];
endmodule

module decoder_4bits (
  input  A3,
  input  Enable,
  input  A2,
  input  A1,
  input  A0,
  output DF,
  output DE,
  output DD,
  output DC,
  output DB,
  output DA,
  output D9,
  output D8,
  output D7,
  output D6,
  output D5,
  output D4,
  output D3,
  output D2,
  output D1,
  output D0
);

  wire and_1_out, and_2_out, and_3_out, and_4_out, and_5_out, and_6_out, and_7_out, and_8_out, and_9_out,
       and_10_out, and_11_out, and_12_out, and_13_out, and_14_out, and_15_out, and_16_out, not_1_out,
       not_2_out, not_3_out, not_4_out;

  not not_1 (not_1_out, A3);
  not not_2 (not_2_out, A2);
  not not_3 (not_3_out, A1);
  not not_4 (not_4_out, A0);
  assign DF = Enable ? and_16_out : 1'bz;  // Controlled_Buffer controlled_buffer_1
  assign DE = Enable ? and_15_out : 1'bz;  // Controlled_Buffer controlled_buffer_2
  and and_1 (and_1_out, not_1_out, not_2_out, not_3_out, not_4_out);
  and and_2 (and_2_out, not_1_out, not_2_out, not_3_out, A0);
  and and_3 (and_3_out, not_1_out, not_2_out, A1, not_4_out);
  and and_4 (and_4_out, not_1_out, not_2_out, A1, A0);
  and and_5 (and_5_out, not_1_out, A2, not_3_out, not_4_out);
  and and_6 (and_6_out, not_1_out, A2, not_3_out, A0);
  and and_7 (and_7_out, not_1_out, A2, A1, not_4_out);
  and and_8 (and_8_out, not_1_out, A2, A1, A0);
  and and_9 (and_9_out, A3, not_2_out, not_3_out, not_4_out);
  and and_10 (and_10_out, A3, not_2_out, not_3_out, A0);
  and and_11 (and_11_out, A3, not_2_out, A1, not_4_out);
  and and_12 (and_12_out, A3, not_2_out, A1, A0);
  and and_13 (and_13_out, A3, A2, not_3_out, not_4_out);
  and and_14 (and_14_out, A3, A2, not_3_out, A0);
  and and_15 (and_15_out, A3, A2, A1, not_4_out);
  and and_16 (and_16_out, A3, A2, A1, A0);
  assign DD = Enable ? and_14_out : 1'bz;  // Controlled_Buffer controlled_buffer_3
  assign DC = Enable ? and_13_out : 1'bz;  // Controlled_Buffer controlled_buffer_4
  assign DB = Enable ? and_12_out : 1'bz;  // Controlled_Buffer controlled_buffer_5
  assign DA = Enable ? and_11_out : 1'bz;  // Controlled_Buffer controlled_buffer_6
  assign D9 = Enable ? and_10_out : 1'bz;  // Controlled_Buffer controlled_buffer_7
  assign D8 = Enable ? and_9_out : 1'bz;  // Controlled_Buffer controlled_buffer_8
  assign D7 = Enable ? and_8_out : 1'bz;  // Controlled_Buffer controlled_buffer_9
  assign D6 = Enable ? and_7_out : 1'bz;  // Controlled_Buffer controlled_buffer_10
  assign D5 = Enable ? and_6_out : 1'bz;  // Controlled_Buffer controlled_buffer_11
  assign D4 = Enable ? and_5_out : 1'bz;  // Controlled_Buffer controlled_buffer_12
  assign D3 = Enable ? and_4_out : 1'bz;  // Controlled_Buffer controlled_buffer_13
  assign D2 = Enable ? and_3_out : 1'bz;  // Controlled_Buffer controlled_buffer_14
  assign D1 = Enable ? and_2_out : 1'bz;  // Controlled_Buffer controlled_buffer_15
  assign D0 = Enable ? and_1_out : 1'bz;  // Controlled_Buffer controlled_buffer_16
endmodule

module SRAM_CIRCUITARY (
  input  d0,
  input  d1,
  input  d2,
  input  d3,
  input  d4,
  input  d5,
  input  d6,
  input  d7,
  input  q0_4,
  input  q1_4,
  input  q2_4,
  input  q3_4,
  input  q0_8,
  input  q1_8,
  input  q2_8,
  input  q3_8,
  input  q0_12,
  input  q1_12,
  input  q2_12,
  input  q3_12,
  input  q0,
  input  q1,
  input  q2,
  input  q3,
  input  q5_4,
  input  q7_8,
  input  q6_12,
  input  q4_12,
  input  q5_12,
  input  q7_12,
  input  q6,
  input  q6_4,
  input  q4_8,
  input  q4,
  input  q5,
  input  q7,
  input  q4_4,
  input  q5_8,
  input  q7_4,
  input  q6_8,
  input  qo_1,
  input  q0_5,
  input  q1_5,
  input  q2_5,
  input  q3_5,
  input  q0_9,
  input  q1_9,
  input  q2_9,
  input  q3_9,
  input  q0_13,
  input  q1_13,
  input  q2_13,
  input  q3_13,
  input  q2_1,
  input  q1_1,
  input  q3_1,
  input  q6_9,
  input  q4_9,
  input  q5_9,
  input  q7_9,
  input  A3,
  input  q6_5,
  input  q4_5,
  input  q5_5,
  input  q7_5,
  input  q6_1,
  input  q6_13,
  input  chip_SEL,
  input  q7_1,
  input  q4_13,
  input  q5_13,
  input  q7_13,
  input  q4_1,
  input  A2,
  input  q5_1,
  input  A1,
  input  A0,
  input  q0_2,
  input  q0_10,
  input  q1_10,
  input  q2_10,
  input  q3_10,
  input  q0_14,
  input  q1_14,
  input  q2_14,
  input  q3_14,
  input  q1_2,
  input  q0_6,
  input  q1_6,
  input  q2_6,
  input  q3_6,
  input  q2_2,
  input  q3_2,
  input  q6_10,
  input  q4_10,
  input  q5_10,
  input  q7_10,
  input  q6_6,
  input  q4_6,
  input  q5_6,
  input  q7_6,
  input  q6_2,
  input  q4_2,
  input  q6_14,
  input  q4_14,
  input  q5_14,
  input  q7_14,
  input  q7_2,
  input  q5_2,
  input  q0_11,
  input  q1_11,
  input  q2_11,
  input  q3_11,
  input  q1_3,
  input  q0_7,
  input  q1_7,
  input  q2_7,
  input  q3_7,
  input  q0_15,
  input  q1_15,
  input  q2_15,
  input  q3_15,
  input  q2_3,
  input  q0_3,
  input  q3_3,
  input  q6_11,
  input  q4_11,
  input  q5_11,
  input  q7_11,
  input  q6_3,
  input  q6_7,
  input  q4_7,
  input  q5_7,
  input  q7_7,
  input  q4_15,
  input  q4_3,
  input  q5_3,
  input  q7_3,
  input  q6_15,
  input  q5_15,
  input  q7_15
);

  wire decoder_4bits_1_d0, decoder_4bits_1_d1, decoder_4bits_1_d2, decoder_4bits_1_d3, decoder_4bits_1_d4,
       decoder_4bits_1_d5, decoder_4bits_1_d6, decoder_4bits_1_d7, decoder_4bits_1_d9, decoder_4bits_1_da,
       decoder_4bits_1_db, decoder_4bits_1_dc, decoder_4bits_1_dd, decoder_4bits_1_de, decoder_4bits_1_df,
       undriven, undriven_2, undriven_3, undriven_4, undriven_5, undriven_6, undriven_7, undriven_8,
       undriven_9, undriven_10, undriven_11, undriven_12, undriven_13, undriven_14, undriven_15, undriven_16,
       undriven_17, undriven_18, undriven_19, undriven_20, undriven_21, undriven_22, undriven_23,
       undriven_24, undriven_25, undriven_26, undriven_27, undriven_28, undriven_29, undriven_30,
       undriven_31, undriven_32, undriven_33, undriven_34, undriven_35, undriven_36, undriven_37,
       undriven_38, undriven_39, undriven_40, undriven_41, undriven_42, undriven_43, undriven_44,
       undriven_45, undriven_46, undriven_47, undriven_48, undriven_49, undriven_50, undriven_51,
       undriven_52, undriven_53, undriven_54, undriven_55, undriven_56, undriven_57, undriven_58,
       undriven_59, undriven_60, undriven_61, undriven_62, undriven_63, undriven_64, undriven_65,
       undriven_66, undriven_67, undriven_68, undriven_69, undriven_70, undriven_71, undriven_72,
       undriven_73, undriven_74, undriven_75, undriven_76, undriven_77, undriven_78, undriven_79,
       undriven_80, undriven_81, undriven_82, undriven_83, undriven_84, undriven_85, undriven_86,
       undriven_87, undriven_88, undriven_89, undriven_90, undriven_91, undriven_92, undriven_93,
       undriven_94, undriven_95, undriven_96, undriven_97, undriven_98, undriven_99, undriven_100,
       undriven_101, undriven_102, undriven_103, undriven_104, undriven_105, undriven_106, undriven_107,
       undriven_108, undriven_109, undriven_110, undriven_111, undriven_112, undriven_113, undriven_114,
       undriven_115, undriven_116, undriven_117, undriven_118, undriven_119, undriven_120;

  decoder_4bits decoder_4bits_1 (
    .A3(A3), .Enable(chip_SEL), .A2(A2), .A1(A1), .A0(A0), .DF(decoder_4bits_1_df), .DE(decoder_4bits_1_de),
    .DD(decoder_4bits_1_dd), .DC(decoder_4bits_1_dc), .DB(decoder_4bits_1_db), .DA(decoder_4bits_1_da),
    .D9(decoder_4bits_1_d9), .D8(d2), .D7(decoder_4bits_1_d7), .D6(decoder_4bits_1_d6),
    .D5(decoder_4bits_1_d5), .D4(decoder_4bits_1_d4), .D3(decoder_4bits_1_d3), .D2(decoder_4bits_1_d2),
    .D1(decoder_4bits_1_d1), .D0(decoder_4bits_1_d0));
  RAM_row ram_row_1 (
    .SEL(decoder_4bits_1_d9), .d2(d2), .d3(d3), .d0(d0), .d1(d0), .q0(q0), .q1(q1), .q2(q2), .q3(undriven),
    .d4(d4), .d6(d3), .d7(d3), .d5(d5), .q6(q6), .q4(undriven_2), .q5(q5), .q7(undriven_3));  // open: EN
  RAM_row ram_row_2 (
    .SEL(d2), .d2(d2), .d3(d3), .d0(d0), .d1(d0), .q0(undriven_14), .q1(undriven_4), .q2(undriven_24),
    .q3(undriven_5), .d4(d4), .d6(d3), .d7(d3), .d5(d5), .q6(undriven_15), .q4(undriven_6), .q5(undriven_7),
    .q7(undriven_25));  // open: EN
  RAM_row ram_row_3 (
    .SEL(decoder_4bits_1_d4), .d2(d2), .d3(d3), .d0(d0), .d1(d0), .q0(undriven_16), .q1(undriven_20),
    .q2(undriven_21), .q3(undriven_8), .d4(d4), .d6(d3), .d7(d3), .d5(d5), .q6(undriven_17),
    .q4(undriven_23), .q5(undriven_9), .q7(undriven_10));  // open: EN
  RAM_row ram_row_4 (
    .SEL(decoder_4bits_1_d0), .d2(d2), .d3(d3), .d0(d0), .d1(d0), .q0(q0_3), .q1(undriven_18),
    .q2(undriven_22), .q3(undriven_11), .d4(d4), .d6(d3), .d7(d3), .d5(d5), .q6(undriven_19),
    .q4(undriven_12), .q5(q5_3), .q7(undriven_13));  // open: EN
  RAM_row ram_row_5 (
    .SEL(decoder_4bits_1_da), .d2(d2), .d3(d3), .d0(d0), .d1(d0), .q0(undriven_36), .q1(undriven_43),
    .q2(undriven_50), .q3(undriven_55), .d4(d4), .d6(d3), .d7(d3), .d5(d5), .q6(undriven_26),
    .q4(undriven_27), .q5(undriven_29), .q7(undriven_28));  // open: EN
  RAM_row ram_row_6 (
    .SEL(decoder_4bits_1_dd), .d2(d2), .d3(d3), .d0(d0), .d1(d0), .q0(undriven_30), .q1(undriven_37),
    .q2(undriven_46), .q3(undriven_53), .d4(d4), .d6(d3), .d7(d3), .d5(d5), .q6(undriven_33),
    .q4(undriven_40), .q5(undriven_47), .q7(undriven_56));  // open: EN
  RAM_row ram_row_7 (
    .SEL(decoder_4bits_1_d5), .d2(d2), .d3(d3), .d0(d0), .d1(d0), .q0(undriven_31), .q1(undriven_38),
    .q2(undriven_44), .q3(undriven_51), .d4(d4), .d6(d3), .d7(d3), .d5(d5), .q6(undriven_34),
    .q4(undriven_41), .q5(undriven_48), .q7(undriven_54));  // open: EN
  RAM_row ram_row_8 (
    .SEL(decoder_4bits_1_d1), .d2(d2), .d3(d3), .d0(d0), .d1(d0), .q0(undriven_32), .q1(undriven_39),
    .q2(undriven_45), .q3(undriven_52), .d4(d4), .d6(d3), .d7(d3), .d5(d5), .q6(undriven_35),
    .q4(undriven_42), .q5(undriven_49), .q7(undriven_57));  // open: EN
  RAM_row ram_row_9 (
    .SEL(decoder_4bits_1_db), .d2(d2), .d3(d3), .d0(d0), .d1(d0), .q0(undriven_63), .q1(undriven_70),
    .q2(undriven_79), .q3(undriven_86), .d4(d4), .d6(d3), .d7(d3), .d5(d5), .q6(undriven_58),
    .q4(undriven_59), .q5(undriven_60), .q7(undriven_61));  // open: EN
  RAM_row ram_row_10 (
    .SEL(decoder_4bits_1_de), .d2(d2), .d3(d3), .d0(d0), .d1(d0), .q0(undriven_62), .q1(undriven_68),
    .q2(undriven_74), .q3(undriven_82), .d4(d4), .d6(d3), .d7(d3), .d5(d5), .q6(undriven_64),
    .q4(undriven_71), .q5(undriven_80), .q7(q7_9));  // open: EN
  RAM_row ram_row_11 (
    .SEL(decoder_4bits_1_d6), .d2(d2), .d3(d3), .d0(d0), .d1(d0), .q0(undriven_69), .q1(undriven_75),
    .q2(undriven_81), .q3(undriven_87), .d4(d4), .d6(d3), .d7(d3), .d5(d5), .q6(undriven_65),
    .q4(undriven_72), .q5(undriven_77), .q7(undriven_83));  // open: EN
  RAM_row ram_row_12 (
    .SEL(decoder_4bits_1_d2), .d2(d2), .d3(d3), .d0(d0), .d1(d0), .q0(undriven_66), .q1(undriven_76),
    .q2(undriven_84), .q3(undriven_88), .d4(d4), .d6(d3), .d7(d3), .d5(d5), .q6(undriven_67),
    .q4(undriven_73), .q5(undriven_78), .q7(undriven_85));  // open: EN
  RAM_row ram_row_13 (
    .SEL(decoder_4bits_1_dc), .d2(d2), .d3(d3), .d0(d0), .d1(d0), .q0(undriven_93), .q1(undriven_101),
    .q2(undriven_108), .q3(undriven_115), .d4(d4), .d6(d3), .d7(d3), .d5(d5), .q6(undriven_97),
    .q4(undriven_105), .q5(undriven_112), .q7(undriven_119));  // open: EN
  RAM_row ram_row_14 (
    .SEL(decoder_4bits_1_df), .d2(d2), .d3(d3), .d0(d0), .d1(d0), .q0(undriven_98), .q1(undriven_106),
    .q2(undriven_113), .q3(undriven_120), .d4(d4), .d6(d3), .d7(d3), .d5(d5), .q6(undriven_94),
    .q4(undriven_102), .q5(undriven_109), .q7(undriven_116));  // open: EN
  RAM_row ram_row_15 (
    .SEL(decoder_4bits_1_d7), .d2(d2), .d3(d3), .d0(d0), .d1(d0), .q0(undriven_92), .q1(undriven_99),
    .q2(undriven_107), .q3(undriven_114), .d4(d4), .d6(d3), .d7(d3), .d5(d5), .q6(undriven_95),
    .q4(undriven_103), .q5(undriven_110), .q7(undriven_117));  // open: EN
  RAM_row ram_row_16 (
    .SEL(decoder_4bits_1_d3), .d2(d2), .d3(d3), .d0(d0), .d1(d0), .q0(undriven_96), .q1(undriven_104),
    .q2(undriven_111), .q3(undriven_118), .d4(d4), .d6(d3), .d7(d3), .d5(d5), .q6(undriven_89),
    .q4(undriven_100), .q5(undriven_90), .q7(undriven_91));  // open: EN

  assign d1 = d0;
  assign d6 = d3;
  assign d7 = d3;
endmodule

module BC (
  input  SEL,
  input  IP,
  input  OP,
  input  EN
);

  wire and_1_out, and_2_out, not_1_out, not_2_out, s_r_ff_1_q;

  not not_1 (not_1_out, IP);
  and and_1 (and_1_out, SEL, not_2_out);
  and and_2 (and_2_out, SEL, not_2_out);
  not not_2 (not_2_out, EN);
  S_R_Flip_Flop s_r_ff_1 (.S(and_1_out), .R(and_2_out), .Q(s_r_ff_1_q));  // open: clk, reset, Qn, preset
  and and_3 (OP, s_r_ff_1_q, SEL);
endmodule

module RAM_row (
  input  SEL,
  input  d2,
  input  d3,
  input  d0,
  input  d1,
  input  q0,
  input  q1,
  input  q2,
  input  q3,
  input  d4,
  input  d6,
  input  d7,
  input  d5,
  input  q6,
  input  q4,
  input  q5,
  input  q7,
  input  EN
);

  wire undriven;

  BC bc_1 (.SEL(SEL), .IP(d0), .OP(undriven), .EN(EN));
  BC bc_2 (.SEL(SEL), .IP(d4), .OP(q4), .EN(EN));
  BC bc_3 (.SEL(SEL), .IP(d1), .OP(q1), .EN(EN));
  BC bc_4 (.IP(d5), .OP(q5), .EN(EN));  // open: SEL
  BC bc_5 (.SEL(SEL), .IP(d2), .OP(q2), .EN(EN));
  BC bc_6 (.SEL(SEL), .IP(d6), .OP(q6), .EN(EN));
  BC bc_7 (.SEL(SEL), .IP(d3), .OP(q3), .EN(EN));
  BC bc_8 (.SEL(SEL), .IP(d7), .OP(EN), .EN(EN));

  assign q7 = EN;
endmodule

module SRAM_CHIP (
  input  [3:0] ADD_IN,
  input  [7:0] DATA_IN,
  input  EA,
  input  SEL,
  output [7:0] RAM_OUT
);

  wire undriven, undriven_2, undriven_3, undriven_4, undriven_5, undriven_6, undriven_7, undriven_8,
       undriven_9, undriven_10, undriven_11, undriven_12, undriven_13, undriven_14, undriven_15, undriven_16,
       undriven_17, undriven_18, undriven_19, undriven_20, undriven_21, undriven_22, undriven_23,
       undriven_24, undriven_25, undriven_26, undriven_27, undriven_28, undriven_29, undriven_30,
       undriven_31, undriven_32, undriven_33, undriven_34, undriven_35, undriven_36, undriven_37,
       undriven_38, undriven_39, undriven_40, undriven_41, undriven_42, undriven_43, undriven_44,
       undriven_45, undriven_46, undriven_47, undriven_48, undriven_49, undriven_50, undriven_51,
       undriven_52, undriven_53, undriven_54, undriven_55, undriven_56, undriven_57, undriven_58,
       undriven_59, undriven_60, undriven_61, undriven_62, undriven_63, undriven_64, undriven_65,
       undriven_67, undriven_68, undriven_69, undriven_70, undriven_71, undriven_72, undriven_73,
       undriven_74, undriven_75, undriven_76, undriven_77, undriven_78, undriven_79, undriven_80,
       undriven_81, undriven_82, undriven_83, undriven_84, undriven_85, undriven_86, undriven_87,
       undriven_88, undriven_89, undriven_90, undriven_91, undriven_92, undriven_93, undriven_94,
       undriven_95, undriven_96, undriven_97, undriven_98, undriven_99, undriven_100, undriven_101,
       undriven_102, undriven_103, undriven_104, undriven_105, undriven_106, undriven_107, undriven_108,
       undriven_109, undriven_110, undriven_111, undriven_112, undriven_113, undriven_114, undriven_115,
       undriven_116, undriven_117, undriven_118, undriven_119, undriven_120, undriven_121, undriven_122,
       undriven_123, undriven_124, undriven_125, undriven_126, undriven_127, undriven_128, undriven_129,
       undriven_130;
  wire [3:0] undriven_66;
  wire [7:0] buffer_2_out, or_1_out;

  assign RAM_OUT = undriven ? or_1_out : 8'bz;  // Controlled_Buffer controlled_buffer_1
  or or_1 (or_1_out[0], undriven_2, undriven_3, undriven_4, undriven_5, undriven_6, undriven_7, undriven_8, undriven_9, undriven_10, undriven_11, undriven_12, undriven_13, undriven_14, undriven_15, undriven_16, undriven_17);
  or or_2 (or_1_out[1], undriven_18, undriven_19, undriven_20, undriven_21, undriven_22, undriven_23, undriven_24, undriven_25, undriven_26, undriven_27, undriven_28, undriven_29, undriven_30, undriven_31, undriven_32, undriven_33);
  or or_3 (or_1_out[2], undriven_34, undriven_35, undriven_36, undriven_37, undriven_38, undriven_39, undriven_40, undriven_41, undriven_42, undriven_43, undriven_44, undriven_45, undriven_46, undriven_47, undriven_48, undriven_49);
  or or_4 (or_1_out[3], undriven_50, undriven_51, undriven_52, undriven_53, undriven_54, undriven_55, undriven_56, undriven_57, undriven_58, undriven_65, undriven_59, undriven_60, undriven_61, undriven_62, undriven_63, undriven_64);
  assign ADD_IN = undriven_66;  // Buffer buffer_1, 4 bits wide
  assign buffer_2_out = DATA_IN;  // Buffer buffer_2, 8 bits wide
  SRAM_CIRCUITARY sram_circuitary_1 (
    .d0(buffer_2_out[0]), .d1(buffer_2_out[1]), .d2(buffer_2_out[2]), .d3(buffer_2_out[3]),
    .d4(buffer_2_out[4]), .d5(buffer_2_out[5]), .d6(buffer_2_out[6]), .d7(buffer_2_out[7]),
    .q0_4(undriven_2), .q1_4(undriven_18), .q2_4(undriven_34), .q3_4(undriven_50), .q0_8(undriven_3),
    .q1_8(undriven_19), .q2_8(undriven_35), .q3_8(undriven_51), .q0_12(undriven_4), .q1_12(undriven_20),
    .q2_12(undriven_36), .q3_12(undriven_52), .q0(undriven_5), .q1(undriven_21), .q2(undriven_37),
    .q3(undriven_53), .q5_4(undriven_68), .q7_8(undriven_91), .q6_12(undriven_69), .q4_12(undriven_70),
    .q5_12(undriven_92), .q7_12(undriven_71), .q6(undriven_72), .q6_4(undriven_73), .q4_8(undriven_74),
    .q4(undriven_93), .q5(undriven_75), .q7(undriven_90), .q4_4(undriven_94), .q5_8(undriven_76),
    .q7_4(undriven_77), .q6_8(undriven_78), .qo_1(undriven_6), .q0_5(undriven_7), .q1_5(undriven_22),
    .q2_5(undriven_38), .q3_5(undriven_54), .q0_9(undriven_8), .q1_9(undriven_23), .q2_9(undriven_39),
    .q3_9(undriven_55), .q0_13(undriven_9), .q1_13(undriven_24), .q2_13(undriven_40), .q3_13(undriven_56),
    .q2_1(undriven_41), .q1_1(undriven_25), .q3_1(undriven_57), .q6_9(undriven_79), .q4_9(undriven_95),
    .q5_9(undriven_80), .q7_9(undriven_67), .A3(undriven_66[3]), .q6_5(undriven_81), .q4_5(undriven_96),
    .q5_5(undriven_107), .q7_5(undriven_117), .q6_1(undriven_82), .q6_13(undriven_83), .chip_SEL(SEL),
    .q7_1(undriven_84), .q4_13(undriven_97), .q5_13(undriven_109), .q7_13(undriven_85), .q4_1(undriven_98),
    .A2(undriven_66[2]), .q5_1(undriven_110), .A1(undriven_66[1]), .A0(undriven_66[0]), .q0_2(undriven_10),
    .q0_10(undriven_14), .q1_10(undriven_26), .q2_10(undriven_42), .q3_10(undriven_58), .q0_14(undriven_11),
    .q1_14(undriven_27), .q2_14(undriven_43), .q3_14(undriven_65), .q1_2(undriven_28), .q0_6(undriven_15),
    .q1_6(undriven_29), .q2_6(undriven_44), .q3_6(undriven_59), .q2_2(undriven_45), .q3_2(undriven_60),
    .q6_10(undriven_108), .q4_10(undriven_99), .q5_10(undriven_111), .q7_10(undriven_86),
    .q6_6(undriven_120), .q4_6(undriven_100), .q5_6(undriven_112), .q7_6(undriven_87), .q6_2(undriven_121),
    .q4_2(undriven_106), .q6_14(undriven_122), .q4_14(undriven_101), .q5_14(undriven_114),
    .q7_14(undriven_88), .q7_2(undriven_89), .q5_2(undriven_115), .q0_11(undriven_17), .q1_11(undriven_30),
    .q2_11(undriven_46), .q3_11(undriven_61), .q1_3(undriven_31), .q0_7(undriven_16), .q1_7(undriven_32),
    .q2_7(undriven_47), .q3_7(undriven_62), .q0_15(undriven_13), .q1_15(undriven_33), .q2_15(undriven_48),
    .q3_15(undriven_63), .q2_3(undriven_49), .q0_3(undriven_12), .q3_3(undriven_64), .q6_11(undriven_123),
    .q4_11(undriven_102), .q5_11(undriven_113), .q7_11(undriven_127), .q6_3(undriven_124),
    .q6_7(undriven_125), .q4_7(undriven_105), .q5_7(undriven_116), .q7_7(undriven_128), .q4_15(undriven_103),
    .q4_3(undriven_104), .q5_3(undriven_119), .q7_3(undriven_129), .q6_15(undriven_126),
    .q5_15(undriven_118), .q7_15(undriven_130));
  or or_5 (or_1_out[4], undriven_70, undriven_93, undriven_94, undriven_95, undriven_96, undriven_97, undriven_98, undriven_99, undriven_100, undriven_101, undriven_102, undriven_103, undriven_104, undriven_105, undriven_106, undriven_74);
  or or_6 (or_1_out[5], undriven_68, undriven_92, undriven_75, undriven_76, undriven_80, undriven_107, undriven_109, undriven_110, undriven_111, undriven_112, undriven_113, undriven_114, undriven_115, undriven_116, undriven_118, undriven_119);
  or or_7 (or_1_out[6], undriven_69, undriven_72, undriven_73, undriven_78, undriven_79, undriven_81, undriven_82, undriven_83, undriven_108, undriven_120, undriven_121, undriven_122, undriven_123, undriven_124, undriven_125, undriven_126);
  or or_8 (or_1_out[7], undriven_91, undriven_71, undriven_90, undriven_77, undriven_67, undriven_84, undriven_87, undriven_85, undriven_86, undriven_88, undriven_117, undriven_89, undriven_127, undriven_128, undriven_129, undriven_130);
endmodule

module IR_CHIP (
  input  [7:0] D_IN,
  input  EA,
  input  EN,
  input  CLK,
  input  n_RESET,
  output [7:0] D_OUT,
  output [3:0] OPCODE,
  output [7:0] operand
);

  wire not_1_out;
  wire [3:0] controlled_buffer_2_out, undriven;

  assign D_IN = EA ? D_IN : 8'bz;  // Controlled_Buffer controlled_buffer_1
  not not_1 (not_1_out, n_RESET);
  Register register_1 (.D(D_IN), .en(EN), .clk(CLK), .Q(D_OUT), .clr(not_1_out));
  Controlled_Buffer #(.width(4)) controlled_buffer_2 (.in(undriven), .out(controlled_buffer_2_out));  // open: en
  assign operand = {{4{controlled_buffer_2_out[3]}}, controlled_buffer_2_out};  // Bit_Extender bit_extender_1
endmodule

module Ring_Counter (
  input  CLK,
  input  reset,
  output [5:0] RC_OUT,
  output T1,
  output T3
);

  wire not_1_out, not_2_out, not_3_out, not_4_out, not_5_out;
  wire [5:0] j_k_ff_1_q;

  J_K_Flip_Flop j_k_ff_1 (.J(j_k_ff_1_q[5]), .clk(CLK), .Q(j_k_ff_1_q[0]), .reset(reset));  // open: K, Qn, preset
  J_K_Flip_Flop j_k_ff_2 (
    .J(j_k_ff_1_q[0]), .K(not_1_out), .clk(CLK), .Q(j_k_ff_1_q[1]), .reset(reset));  // open: Qn, preset
  not not_1 (not_1_out, j_k_ff_1_q[0]);
  J_K_Flip_Flop j_k_ff_3 (
    .J(j_k_ff_1_q[1]), .K(not_2_out), .clk(CLK), .Q(j_k_ff_1_q[2]), .reset(reset));  // open: Qn, preset
  not not_2 (not_2_out, j_k_ff_1_q[1]);
  J_K_Flip_Flop j_k_ff_4 (
    .J(j_k_ff_1_q[2]), .K(not_3_out), .clk(CLK), .Q(j_k_ff_1_q[3]), .reset(reset));  // open: Qn, preset
  not not_3 (not_3_out, j_k_ff_1_q[2]);
  J_K_Flip_Flop j_k_ff_5 (
    .J(j_k_ff_1_q[3]), .K(not_4_out), .clk(CLK), .Q(j_k_ff_1_q[4]), .reset(reset));  // open: Qn, preset
  not not_4 (not_4_out, j_k_ff_1_q[3]);
  J_K_Flip_Flop j_k_ff_6 (
    .J(j_k_ff_1_q[4]), .K(not_5_out), .clk(CLK), .Q(j_k_ff_1_q[5]), .reset(reset));  // open: Qn, preset
  not not_5 (not_5_out, j_k_ff_1_q[4]);
  assign RC_OUT = j_k_ff_1_q;  // Buffer buffer_1, 6 bits wide
endmodule

module MCPG_CONTROL (
  input  T1,
  input  T3,
  input  [11:0] OUT_ROM,
  input  [3:0] IN_ROM,
  input  CLK,
  output B11,
  output B10,
  output B9,
  output B8,
  output B7,
  output B6,
  output B5,
  output B4,
  output B3,
  output B2,
  output B1,
  output B0
);

  wire [3:0] ADD_ROM_data, PS_COUNTER_q;

  ROM #(.addrWidth(4), .dataWidth(4)) ADD_ROM (.addr(IN_ROM), .data(ADD_ROM_data));
  Counter #(.max('hf), .width(4)) PS_COUNTER (
    .clr(T1), .load(T3), .up(1'b1), .count(1'b1), .clk(CLK), .D(ADD_ROM_data), .Q(PS_COUNTER_q));  // open: carry
  ROM #(.addrWidth(4), .dataWidth(12)) rom_1 (.addr(PS_COUNTER_q), .data(OUT_ROM));

  // Notes on the sheet:
  //   contents of ADD_ROM (hex, n*v repeats v):
  //   3 6 9 11*0 c f
  //   contents of rom_1 (hex, n*v repeats v):
  //   5e3 be3 263 1a3 2c3 3e3 1a3 2e1 3c7 1a3 2e1 3cf 3f2 3e3 3e3
endmodule
